// Logisim project project_logism.circ as structural Verilog: 1 circuit, main circuit main
module main (
  input  A,
  input  B,
  input  C,
  input  A_2,
  input  B_2,
  input  C_2
);

  wire and_1_out, and_2_out, and_3_out, nand_1_out, nand_2_out, nand_3_out, nand_4_out, nand_5_out, or_1_out;

  and and_1 (and_1_out, A, ~B);  // AND_Gate
  and and_2 (and_2_out, ~B, C);  // AND_Gate
  and and_3 (and_3_out, B, C);
  nand nand_1 (nand_1_out, B_2, B_2);
  nand nand_2 (nand_2_out, A_2, nand_1_out);
  nand nand_3 (nand_3_out, nand_1_out, C_2);
  nand nand_4 (nand_4_out, B_2, C_2);
  or or_1 (or_1_out, and_1_out, and_2_out, and_3_out);
  LED f_A_B_C (.in(or_1_out));
  nand nand_5 (nand_5_out, nand_2_out, nand_3_out, nand_4_out);
  LED f_A_B_C_2 (.in(nand_5_out));

  // Notes on the sheet:
  //   AND-OR Digital Circuit
  //   NAND Digital Circuit
endmodule
